// Logisim project cpu.circ as structural Verilog: 9 circuits, main circuit main
module main (
  input  Reset
);

  wire add, addi, ALUSrc, ALUsub, and_1_out, and_2_out, and_gate, Available, beq, bgez, clk, eqz, gez,
       input_data, j, jal, jr, lw, memory_latch_1_oe_latched, memory_latch_1_we_latched, not_1_out,
       not_4_out, not_gate, or_8_out, or_9_out, output_data, RegDst, RegWrite, shift_ll, shift_rl, sub, sw;
  wire [2:0] ALUCtrl, d, multiplexer_3_out;
  wire [6:0] keyboard_out;
  wire [11:0] Address;
  wire [15:0] adder_full_1_result, adder_full_2_result, ALUOut, bit_extender_1_out, bit_extender_2_out,
       bit_extender_3_out, Data_new, mem_in, memory_latch_1_address_latched, memory_latch_1_data_in_latched,
       multiplexer_1_out, multiplexer_2_out, multiplexer_4_out, multiplexer_6_out, multiplexer_7_out,
       multiplexer_8_out, multiplexer_9_out, not_3_out, Program_Counter_dataout, ram_1_dout,
       Register_File_readdata2;
  wire [15:12] Instructions;

  Clock clock_1 (.out(clk));
  or or_1 (ALUCtrl[1], addi, sub, add, not_gate, lw, sw, bgez, beq);
  or or_2 (ALUCtrl[0], sw, lw, addi, sub, add, shift_rl, bgez, beq);
  or or_3 (ALUCtrl[2], shift_ll, shift_rl);
  not not_1 (not_1_out, clk);
  or or_4 (ALUSrc, addi, lw, sw, bgez);
  or or_5 (ALUsub, sub, bgez, beq);
  register_onebit Program_Counter (
    .clk(not_1_out), .write_enable(1'b1), .reset(Reset), .datain(multiplexer_8_out),
    .dataout(Program_Counter_dataout));
  ROM #(.addrWidth(16), .dataWidth(16)) Instruction_Memory (
    .addr(Program_Counter_dataout), .data({Instructions, Address}));
  adder_full adder_full_1 (.A(16'h1), .B(Program_Counter_dataout), .result(adder_full_1_result));  // open: sub, ovf
  Multiplexer #(.width(16), .enable("false")) multiplexer_1 (
    .in0(multiplexer_9_out), .in1(adder_full_1_result), .out(multiplexer_1_out), .sel(jal));
  or or_6 (RegWrite, addi, sub, add, not_gate, and_gate, shift_ll, shift_rl, lw, jal, input_data);
  or or_7 (RegDst, sub, add, not_gate, and_gate, shift_ll, shift_rl, input_data);
  Multiplexer #(.width(16), .enable("false")) multiplexer_2 (
    .in0(multiplexer_1_out), .in1(Data_new), .out(multiplexer_2_out), .sel(input_data));
  // Probe on multiplexer_2_out
  // Probe on multiplexer_9_out
  RegisterFile Register_File (
    .WriteData(multiplexer_2_out), .clk(clk), .Reset(Reset), .ReadReg1(Address[11:9]),
    .RegWriteEnable(RegWrite), .WriteReg(d), .ReadReg2(Address[8:6]), .ReadData1(mem_in),
    .ReadData2(Register_File_readdata2));
  assign bit_extender_1_out = {{10{Address[5]}}, Address[5:0]};  // Bit_Extender bit_extender_1
  Multiplexer #(.width(3), .enable("false")) multiplexer_3 (
    .in0(Address[8:6]), .in1(Address[5:3]), .out(multiplexer_3_out), .sel(RegDst));
  Decoder #(.select(4), .enable("false")) decoder_1 (
    .out0(addi), .out1(sub), .out2(add), .out3(not_gate), .out4(and_gate), .out5(shift_ll), .out6(shift_rl),
    .out7(lw), .out8(sw), .out9(bgez), .out10(beq), .out11(j), .out12(jr), .out13(jal), .out14(input_data),
    .out15(output_data), .sel(Instructions));
  // Probe on mem_in
  Multiplexer #(.width(16), .enable("false")) multiplexer_4 (
    .in0(Register_File_readdata2), .in1(bit_extender_1_out), .out(multiplexer_4_out), .sel(ALUSrc));
  Multiplexer #(.width(3), .enable("false")) multiplexer_5 (.in0(multiplexer_3_out), .in1(3'b111), .out(d), .sel(jal));
  adder_full adder_full_2 (
    .A(adder_full_1_result), .B(bit_extender_1_out), .result(adder_full_2_result));  // open: sub, ovf
  not not_2 (gez, mem_in[15]);
  and and_1 (and_1_out, beq, eqz);
  or or_8 (or_8_out, and_1_out, and_2_out);
  and and_2 (and_2_out, bgez, gez);
  ALU alu_1 (
    .A(mem_in), .B(multiplexer_4_out), .F(ALUCtrl), .sub(ALUsub), .shamt(Address[2:0]), .Result(ALUOut));  // open: Cout
  Multiplexer #(.width(16), .enable("false")) multiplexer_6 (
    .in0(adder_full_1_result), .in1(adder_full_2_result), .out(multiplexer_6_out), .sel(or_8_out));
  assign bit_extender_2_out = {{4{Address[11]}}, Address};  // Bit_Extender bit_extender_2
  assign not_3_out = ~ALUOut;  // NOT_Gate not_3, 16 bits wide
  Multiplexer #(.width(16), .enable("false")) multiplexer_7 (
    .in0(multiplexer_6_out), .in1(bit_extender_2_out), .out(multiplexer_7_out), .sel(or_9_out));
  or or_9 (or_9_out, j, jal);
  not not_4 (not_4_out, clk);
  Multiplexer #(.width(16), .enable("false")) multiplexer_8 (
    .in0(multiplexer_7_out), .in1(mem_in), .out(multiplexer_8_out), .sel(jr));
  and and_3 (eqz, not_3_out[0], not_3_out[1], not_3_out[2], not_3_out[3], not_3_out[4], not_3_out[5], not_3_out[6], not_3_out[7], not_3_out[8], not_3_out[9], not_3_out[10], not_3_out[11], not_3_out[12], not_3_out[13], not_3_out[14], not_3_out[15]);
  memory_latch memory_latch_1 (
    .address(ALUOut), .WE(sw), .clk(not_4_out), .data_in(Register_File_readdata2),
    .address_latched(memory_latch_1_address_latched), .WE_latched(memory_latch_1_we_latched),
    .OE_latched(memory_latch_1_oe_latched), .data_in_latched(memory_latch_1_data_in_latched));
  RAM #(.addrWidth(16), .dataWidth(16), .trigger("high"), .databus("bibus")) ram_1 (
    .addr(memory_latch_1_address_latched), .we(memory_latch_1_we_latched), .oe(memory_latch_1_oe_latched),
    .din(memory_latch_1_data_in_latched), .dout(ram_1_dout));
  Keyboard #(.trigger("falling")) keyboard_1 (
    .clk(clk), .re(input_data), .clr(Reset), .avail(Available), .data(keyboard_out));
  TTY #(.rows(13), .cols(80)) tty_1 (.data(mem_in[6:0]), .clk(clk), .we(output_data), .clr(Reset));
  Multiplexer #(.width(16), .enable("false")) multiplexer_9 (
    .in0(ALUOut), .in1(ram_1_dout), .out(multiplexer_9_out), .sel(lw));
  Multiplexer #(.width(16), .enable("false")) multiplexer_10 (
    .in0(16'h80), .in1(bit_extender_3_out), .out(Data_new), .sel(Available));
  assign bit_extender_3_out = {{9{1'b0}}, keyboard_out};  // Bit_Extender bit_extender_3

  // Other names for the same wires on the sheet: Immediate[5:0] = Address[5:0]; Instructions[11:0] = Address;
  //   shamt[2:0] = Address[2:0]; Rd[2:0] = Address[5:3]; Rt[2:0] = Address[8:6]; Rs[2:0] = Address[11:9];
  //   Opcode[3:0] = Instructions; mem_out[6:0] = mem_in[6:0]; R = Reset

  // Notes on the sheet:
  //   contents of Instruction_Memory (hex, n*v repeats v):
  //   4b 8c cd 10c 141 a446 142 a4c6 143 a506 197 903f 19e 903f 19f 903f 41 144 9202 198 903f 145 7f 9212
  //   146 40 9202 199 903f 147 b021 19a 903f 148 d025 14a 903f 242 149 ce00 19b 903f 19c 903f 6822 6822
  //   6822 6823 6824 6823 6*0 903f
endmodule

module adder_full (
  input  sub,
  input  [15:0] A,
  input  [15:0] B,
  output ovf,
  output [15:0] result
);

  wire adder_onebit_1_cout, adder_onebit_2_cout, adder_onebit_3_cout, adder_onebit_4_cout,
       adder_onebit_5_cout, adder_onebit_6_cout, adder_onebit_7_cout, adder_onebit_8_cout,
       adder_onebit_9_cout, adder_onebit_10_cout, adder_onebit_11_cout, adder_onebit_12_cout,
       adder_onebit_13_cout, adder_onebit_14_cout, adder_onebit_15_cout, adder_onebit_16_cout, xor_1_out,
       xor_2_out, xor_3_out, xor_4_out, xor_5_out, xor_6_out, xor_7_out, xor_8_out, xor_9_out, xor_10_out,
       xor_11_out, xor_12_out, xor_13_out, xor_14_out, xor_15_out, xor_16_out;

  xor xor_1 (xor_1_out, sub, A[15]);
  xor xor_2 (xor_2_out, sub, A[14]);
  xor xor_3 (xor_3_out, sub, A[13]);
  xor xor_4 (xor_4_out, sub, A[12]);
  xor xor_5 (xor_5_out, sub, A[11]);
  xor xor_6 (xor_6_out, sub, A[10]);
  xor xor_7 (xor_7_out, sub, A[9]);
  xor xor_8 (xor_8_out, sub, A[8]);
  xor xor_9 (xor_9_out, sub, A[7]);
  xor xor_10 (xor_10_out, sub, A[6]);
  xor xor_11 (xor_11_out, sub, A[5]);
  xor xor_12 (xor_12_out, sub, A[4]);
  xor xor_13 (xor_13_out, sub, A[3]);
  xor xor_14 (xor_14_out, sub, A[2]);
  xor xor_15 (xor_15_out, sub, A[1]);
  xor xor_16 (xor_16_out, sub, A[0]);
  adder_onebit adder_onebit_1 (
    .Cin(adder_onebit_2_cout), .A(xor_1_out), .B(B[15]), .sum(result[15]), .Cout(adder_onebit_1_cout));
  adder_onebit adder_onebit_2 (
    .Cin(adder_onebit_3_cout), .A(xor_2_out), .B(B[14]), .sum(result[14]), .Cout(adder_onebit_2_cout));
  adder_onebit adder_onebit_3 (
    .Cin(adder_onebit_4_cout), .A(xor_3_out), .B(B[13]), .sum(result[13]), .Cout(adder_onebit_3_cout));
  adder_onebit adder_onebit_4 (
    .Cin(adder_onebit_5_cout), .A(xor_4_out), .B(B[12]), .sum(result[12]), .Cout(adder_onebit_4_cout));
  adder_onebit adder_onebit_5 (
    .Cin(adder_onebit_6_cout), .A(xor_5_out), .B(B[11]), .sum(result[11]), .Cout(adder_onebit_5_cout));
  adder_onebit adder_onebit_6 (
    .Cin(adder_onebit_7_cout), .A(xor_6_out), .B(B[10]), .sum(result[10]), .Cout(adder_onebit_6_cout));
  adder_onebit adder_onebit_7 (
    .Cin(adder_onebit_8_cout), .A(xor_7_out), .B(B[9]), .sum(result[9]), .Cout(adder_onebit_7_cout));
  adder_onebit adder_onebit_8 (
    .Cin(adder_onebit_9_cout), .A(xor_8_out), .B(B[8]), .sum(result[8]), .Cout(adder_onebit_8_cout));
  adder_onebit adder_onebit_9 (
    .Cin(adder_onebit_10_cout), .A(xor_9_out), .B(B[7]), .sum(result[7]), .Cout(adder_onebit_9_cout));
  adder_onebit adder_onebit_10 (
    .Cin(adder_onebit_11_cout), .A(xor_10_out), .B(B[6]), .sum(result[6]), .Cout(adder_onebit_10_cout));
  adder_onebit adder_onebit_11 (
    .Cin(adder_onebit_12_cout), .A(xor_11_out), .B(B[5]), .sum(result[5]), .Cout(adder_onebit_11_cout));
  adder_onebit adder_onebit_12 (
    .Cin(adder_onebit_13_cout), .A(xor_12_out), .B(B[4]), .sum(result[4]), .Cout(adder_onebit_12_cout));
  adder_onebit adder_onebit_13 (
    .Cin(adder_onebit_14_cout), .A(xor_13_out), .B(B[3]), .sum(result[3]), .Cout(adder_onebit_13_cout));
  adder_onebit adder_onebit_14 (
    .Cin(adder_onebit_15_cout), .A(xor_14_out), .B(B[2]), .sum(result[2]), .Cout(adder_onebit_14_cout));
  adder_onebit adder_onebit_15 (
    .Cin(adder_onebit_16_cout), .A(xor_15_out), .B(B[1]), .sum(result[1]), .Cout(adder_onebit_15_cout));
  adder_onebit adder_onebit_16 (.Cin(sub), .A(xor_16_out), .B(B[0]), .sum(result[0]), .Cout(adder_onebit_16_cout));
  xor xor_17 (ovf, adder_onebit_1_cout, adder_onebit_2_cout);
endmodule

module adder_onebit (
  input  Cin,
  input  A,
  input  B,
  output sum,
  output Cout
);

  wire and_1_out, and_2_out, xor_1_out;

  and and_1 (and_1_out, B, A);
  xor xor_1 (xor_1_out, A, B);
  and and_2 (and_2_out, xor_1_out, Cin);
  or or_1 (Cout, and_1_out, and_2_out);
  xor xor_2 (sum, Cin, xor_1_out);
endmodule

module ALU (
  input  [15:0] A,
  input  [15:0] B,
  input  [2:0] F,
  input  sub,
  input  [2:0] shamt,
  output [15:0] Result,
  output Cout
);

  wire [15:0] adder_full_1_result, and_1_out, not_1_out, or_1_out, shiftleft_1_dataout, shiftright_1_dataout;

  assign and_1_out = B & A;  // AND_Gate and_1, 16 bits wide
  assign or_1_out = B | A;  // OR_Gate or_1, 16 bits wide
  assign not_1_out = ~A;  // NOT_Gate not_1, 16 bits wide
  adder_full adder_full_1 (.sub(sub), .A(B), .B(A), .ovf(Cout), .result(adder_full_1_result));
  shiftLeft shiftleft_1 (.Shifter(shamt), .Datain(A), .Dataout(shiftleft_1_dataout));
  shiftRight shiftright_1 (.Shifter(shamt), .Datain(A), .Dataout(shiftright_1_dataout));
  Multiplexer #(.select(3), .width(16), .enable("false")) multiplexer_1 (
    .in0(and_1_out), .in1(or_1_out), .in2(not_1_out), .in3(adder_full_1_result), .in4(shiftleft_1_dataout),
    .in5(shiftright_1_dataout), .out(Result), .sel(F));  // open: in6, in7
endmodule

module register_onebit (
  input  clk,
  input  write_enable,
  input  reset,
  input  [15:0] datain,
  output [15:0] dataout
);

  wire clkwe;

  and and_1 (clkwe, clk, write_enable);
  D_Flip_Flop d_ff_1 (.D(datain[0]), .clk(clkwe), .Q(dataout[0]), .reset(reset));  // open: Qn, preset
  D_Flip_Flop d_ff_2 (.D(datain[1]), .clk(clkwe), .Q(dataout[1]), .reset(reset));  // open: Qn, preset
  D_Flip_Flop d_ff_3 (.D(datain[2]), .clk(clkwe), .Q(dataout[2]), .reset(reset));  // open: Qn, preset
  D_Flip_Flop d_ff_4 (.D(datain[3]), .clk(clkwe), .Q(dataout[3]), .reset(reset));  // open: Qn, preset
  D_Flip_Flop d_ff_5 (.D(datain[4]), .clk(clkwe), .Q(dataout[4]), .reset(reset));  // open: Qn, preset
  D_Flip_Flop d_ff_6 (.D(datain[5]), .clk(clkwe), .Q(dataout[5]), .reset(reset));  // open: Qn, preset
  D_Flip_Flop d_ff_7 (.D(datain[6]), .clk(clkwe), .Q(dataout[6]), .reset(reset));  // open: Qn, preset
  D_Flip_Flop d_ff_8 (.D(datain[7]), .clk(clkwe), .Q(dataout[7]), .reset(reset));  // open: Qn, preset
  D_Flip_Flop d_ff_9 (.D(datain[8]), .clk(clkwe), .Q(dataout[8]), .reset(reset));  // open: Qn, preset
  D_Flip_Flop d_ff_10 (.D(datain[9]), .clk(clkwe), .Q(dataout[9]), .reset(reset));  // open: Qn, preset
  D_Flip_Flop d_ff_11 (.D(datain[10]), .clk(clkwe), .Q(dataout[10]), .reset(reset));  // open: Qn, preset
  D_Flip_Flop d_ff_12 (.D(datain[11]), .clk(clkwe), .Q(dataout[11]), .reset(reset));  // open: Qn, preset
  D_Flip_Flop d_ff_13 (.D(datain[12]), .clk(clkwe), .Q(dataout[12]), .reset(reset));  // open: Qn, preset
  D_Flip_Flop d_ff_14 (.D(datain[13]), .clk(clkwe), .Q(dataout[13]), .reset(reset));  // open: Qn, preset
  D_Flip_Flop d_ff_15 (.D(datain[14]), .clk(clkwe), .Q(dataout[14]), .reset(reset));  // open: Qn, preset
  D_Flip_Flop d_ff_16 (.D(datain[15]), .clk(clkwe), .Q(dataout[15]), .reset(reset));  // open: Qn, preset

  // Other names for the same wires on the sheet: a0 = datain[0]; a1 = datain[1]; a2 = datain[2]; a3 = datain[3];
  //   a4 = datain[4]; a5 = datain[5]; a6 = datain[6]; a7 = datain[7]; a8 = datain[8]; a9 = datain[9];
  //   a10 = datain[10]; a11 = datain[11]; a12 = datain[12]; a13 = datain[13]; a14 = datain[14]; a15 = datain[15];
  //   b0 = dataout[0]; b1 = dataout[1]; b2 = dataout[2]; b3 = dataout[3]; b4 = dataout[4]; b5 = dataout[5];
  //   b6 = dataout[6]; b7 = dataout[7]; b8 = dataout[8]; b9 = dataout[9]; b10 = dataout[10]; b11 = dataout[11];
  //   b12 = dataout[12]; b13 = dataout[13]; b14 = dataout[14]; b15 = dataout[15]; R = reset
endmodule

module RegisterFile (
  input  [15:0] WriteData,
  input  clk,
  input  Reset,
  input  [2:0] ReadReg1,
  input  RegWriteEnable,
  input  [2:0] WriteReg,
  input  [2:0] ReadReg2,
  output [15:0] ReadData1,
  output [15:0] ReadData2
);

  wire Read1_0, Read1_1, Read1_2, Read1_3, Read1_4, Read1_5, Read1_6, Read1_7, Read2_0, Read2_1, Read2_2,
       Read2_3, Read2_4, Read2_5, Read2_6, Read2_7, Write0, Write1, Write2, Write3, Write4, Write5, Write6,
       Write7;
  wire [15:0] register_onebit_1_dataout, register_onebit_2_dataout, register_onebit_3_dataout,
       register_onebit_4_dataout, register_onebit_5_dataout, register_onebit_6_dataout,
       register_onebit_7_dataout;

  Decoder #(.select(3)) decoder_1 (
    .out0(Write0), .out1(Write1), .out2(Write2), .out3(Write3), .out4(Write4), .out5(Write5), .out6(Write6),
    .out7(Write7), .sel(WriteReg), .en(RegWriteEnable));
  // Probe on {16{1'b0}}
  // Probe on register_onebit_1_dataout
  register_onebit register_onebit_1 (
    .clk(clk), .write_enable(Write1), .reset(Reset), .datain(WriteData), .dataout(register_onebit_1_dataout));
  register_onebit register_onebit_2 (
    .clk(clk), .write_enable(Write2), .reset(Reset), .datain(WriteData), .dataout(register_onebit_2_dataout));
  // Probe on register_onebit_2_dataout
  register_onebit register_onebit_3 (
    .clk(clk), .write_enable(Write3), .reset(Reset), .datain(WriteData), .dataout(register_onebit_3_dataout));
  // Probe on register_onebit_3_dataout
  register_onebit register_onebit_4 (
    .clk(clk), .write_enable(Write4), .reset(Reset), .datain(WriteData), .dataout(register_onebit_4_dataout));
  // Probe on register_onebit_4_dataout
  register_onebit register_onebit_5 (
    .clk(clk), .write_enable(Write5), .reset(Reset), .datain(WriteData), .dataout(register_onebit_5_dataout));
  // Probe on register_onebit_5_dataout
  register_onebit register_onebit_6 (
    .clk(clk), .write_enable(Write6), .reset(Reset), .datain(WriteData), .dataout(register_onebit_6_dataout));
  // Probe on register_onebit_6_dataout
  register_onebit register_onebit_7 (
    .clk(clk), .write_enable(Write7), .reset(Reset), .datain(WriteData), .dataout(register_onebit_7_dataout));
  // Probe on register_onebit_7_dataout
  // Probe on register_onebit_2_dataout
  assign ReadData1 = Read1_0 ? {16{1'b0}} : 16'bz;  // Controlled_Buffer controlled_buffer_1
  assign ReadData2 = Read2_0 ? {16{1'b0}} : 16'bz;  // Controlled_Buffer controlled_buffer_2
  assign ReadData1 = Read1_1 ? register_onebit_1_dataout : 16'bz;  // Controlled_Buffer controlled_buffer_3
  assign ReadData2 = Read2_1 ? register_onebit_1_dataout : 16'bz;  // Controlled_Buffer controlled_buffer_4
  assign ReadData1 = Read1_2 ? register_onebit_2_dataout : 16'bz;  // Controlled_Buffer controlled_buffer_5
  assign ReadData2 = Read2_2 ? register_onebit_2_dataout : 16'bz;  // Controlled_Buffer controlled_buffer_6
  assign ReadData1 = Read1_3 ? register_onebit_3_dataout : 16'bz;  // Controlled_Buffer controlled_buffer_7
  assign ReadData2 = Read2_3 ? register_onebit_3_dataout : 16'bz;  // Controlled_Buffer controlled_buffer_8
  assign ReadData1 = Read1_4 ? register_onebit_4_dataout : 16'bz;  // Controlled_Buffer controlled_buffer_9
  assign ReadData2 = Read2_4 ? register_onebit_4_dataout : 16'bz;  // Controlled_Buffer controlled_buffer_10
  assign ReadData1 = Read1_5 ? register_onebit_5_dataout : 16'bz;  // Controlled_Buffer controlled_buffer_11
  assign ReadData2 = Read2_5 ? register_onebit_5_dataout : 16'bz;  // Controlled_Buffer controlled_buffer_12
  assign ReadData1 = Read1_6 ? register_onebit_6_dataout : 16'bz;  // Controlled_Buffer controlled_buffer_13
  assign ReadData2 = Read2_6 ? register_onebit_6_dataout : 16'bz;  // Controlled_Buffer controlled_buffer_14
  assign ReadData1 = Read1_7 ? register_onebit_7_dataout : 16'bz;  // Controlled_Buffer controlled_buffer_15
  assign ReadData2 = Read2_7 ? register_onebit_7_dataout : 16'bz;  // Controlled_Buffer controlled_buffer_16
  Decoder #(.select(3)) decoder_2 (
    .out0(Read1_0), .out1(Read1_1), .out2(Read1_2), .out3(Read1_3), .out4(Read1_4), .out5(Read1_5),
    .out6(Read1_6), .out7(Read1_7), .sel(ReadReg1));  // open: en
  Decoder #(.select(3)) decoder_3 (
    .out0(Read2_0), .out1(Read2_1), .out2(Read2_2), .out3(Read2_3), .out4(Read2_4), .out5(Read2_5),
    .out6(Read2_6), .out7(Read2_7), .sel(ReadReg2));  // open: en

  // Other names for the same wires on the sheet: R = Reset
endmodule

module memory_latch (
  input  [15:0] address,
  input  WE,
  input  clk,
  input  [15:0] data_in,
  output [15:0] address_latched,
  output WE_latched,
  output OE_latched,
  output [15:0] data_in_latched
);

  wire DMwe_latch_q;
  wire [15:0] addr_latch_q;

  Register #(.width(16), .trigger("falling")) addr_latch (
    .D(address), .en(WE), .clk(clk), .Q(addr_latch_q));  // open: clr
  Register #(.width(16), .trigger("falling")) data_to_be_written (
    .D(data_in), .en(WE), .clk(clk), .Q(data_in_latched));  // open: clr
  D_Flip_Flop #(.trigger("falling")) DMwe_latch (.D(WE), .clk(clk), .Q(DMwe_latch_q));  // open: Qn, preset, reset
  Multiplexer #(.width(16), .enable("false")) multiplexer_1 (
    .in0(address), .in1(addr_latch_q), .out(address_latched), .sel(DMwe_latch_q));
  and and_1 (WE_latched, clk, DMwe_latch_q);
  not not_1 (OE_latched, WE_latched);
endmodule

module shiftLeft (
  input  [2:0] Shifter,
  input  [15:0] Datain,
  output [15:0] Dataout
);

  wire multiplexer_1_out, multiplexer_2_out, multiplexer_3_out, multiplexer_4_out, multiplexer_5_out,
       multiplexer_6_out, multiplexer_7_out, multiplexer_8_out, multiplexer_9_out, multiplexer_10_out,
       multiplexer_11_out, multiplexer_12_out, multiplexer_13_out, multiplexer_14_out, multiplexer_15_out,
       multiplexer_16_out, multiplexer_17_out, multiplexer_18_out, multiplexer_19_out, multiplexer_20_out,
       multiplexer_21_out, multiplexer_22_out, multiplexer_23_out, multiplexer_24_out, multiplexer_25_out,
       multiplexer_26_out, multiplexer_27_out, multiplexer_28_out, multiplexer_29_out, multiplexer_30_out,
       multiplexer_31_out, multiplexer_32_out;

  Multiplexer #(.enable("false")) multiplexer_1 (
    .in0(Datain[15]), .in1(Datain[14]), .out(multiplexer_1_out), .sel(Shifter[0]));
  Multiplexer #(.enable("false")) multiplexer_2 (
    .in0(Datain[14]), .in1(Datain[13]), .out(multiplexer_2_out), .sel(Shifter[0]));
  Multiplexer #(.enable("false")) multiplexer_3 (
    .in0(Datain[13]), .in1(Datain[12]), .out(multiplexer_3_out), .sel(Shifter[0]));
  Multiplexer #(.enable("false")) multiplexer_4 (
    .in0(Datain[12]), .in1(Datain[11]), .out(multiplexer_4_out), .sel(Shifter[0]));
  Multiplexer #(.enable("false")) multiplexer_5 (
    .in0(Datain[11]), .in1(Datain[10]), .out(multiplexer_5_out), .sel(Shifter[0]));
  Multiplexer #(.enable("false")) multiplexer_6 (
    .in0(Datain[10]), .in1(Datain[9]), .out(multiplexer_6_out), .sel(Shifter[0]));
  Multiplexer #(.enable("false")) multiplexer_7 (
    .in0(Datain[9]), .in1(Datain[8]), .out(multiplexer_7_out), .sel(Shifter[0]));
  Multiplexer #(.enable("false")) multiplexer_8 (
    .in0(Datain[8]), .in1(Datain[7]), .out(multiplexer_8_out), .sel(Shifter[0]));
  Multiplexer #(.enable("false")) multiplexer_9 (
    .in0(Datain[7]), .in1(Datain[6]), .out(multiplexer_9_out), .sel(Shifter[0]));
  Multiplexer #(.enable("false")) multiplexer_10 (
    .in0(Datain[6]), .in1(Datain[5]), .out(multiplexer_10_out), .sel(Shifter[0]));
  Multiplexer #(.enable("false")) multiplexer_11 (
    .in0(Datain[5]), .in1(Datain[4]), .out(multiplexer_11_out), .sel(Shifter[0]));
  Multiplexer #(.enable("false")) multiplexer_12 (
    .in0(Datain[4]), .in1(Datain[3]), .out(multiplexer_12_out), .sel(Shifter[0]));
  Multiplexer #(.enable("false")) multiplexer_13 (
    .in0(Datain[3]), .in1(Datain[2]), .out(multiplexer_13_out), .sel(Shifter[0]));
  Multiplexer #(.enable("false")) multiplexer_14 (
    .in0(Datain[2]), .in1(Datain[1]), .out(multiplexer_14_out), .sel(Shifter[0]));
  Multiplexer #(.enable("false")) multiplexer_15 (
    .in0(Datain[1]), .in1(Datain[0]), .out(multiplexer_15_out), .sel(Shifter[0]));
  Multiplexer #(.enable("false")) multiplexer_16 (
    .in0(Datain[0]), .in1(1'b0), .out(multiplexer_16_out), .sel(Shifter[0]));
  Multiplexer #(.enable("false")) multiplexer_17 (
    .in0(multiplexer_1_out), .in1(multiplexer_3_out), .out(multiplexer_17_out), .sel(Shifter[1]));
  Multiplexer #(.enable("false")) multiplexer_18 (
    .in0(multiplexer_2_out), .in1(multiplexer_4_out), .out(multiplexer_18_out), .sel(Shifter[1]));
  Multiplexer #(.enable("false")) multiplexer_19 (
    .in0(multiplexer_3_out), .in1(multiplexer_5_out), .out(multiplexer_19_out), .sel(Shifter[1]));
  Multiplexer #(.enable("false")) multiplexer_20 (
    .in0(multiplexer_4_out), .in1(multiplexer_6_out), .out(multiplexer_20_out), .sel(Shifter[1]));
  Multiplexer #(.enable("false")) multiplexer_21 (
    .in0(multiplexer_5_out), .in1(multiplexer_7_out), .out(multiplexer_21_out), .sel(Shifter[1]));
  Multiplexer #(.enable("false")) multiplexer_22 (
    .in0(multiplexer_6_out), .in1(multiplexer_8_out), .out(multiplexer_22_out), .sel(Shifter[1]));
  Multiplexer #(.enable("false")) multiplexer_23 (
    .in0(multiplexer_7_out), .in1(multiplexer_9_out), .out(multiplexer_23_out), .sel(Shifter[1]));
  Multiplexer #(.enable("false")) multiplexer_24 (
    .in0(multiplexer_8_out), .in1(multiplexer_10_out), .out(multiplexer_24_out), .sel(Shifter[1]));
  Multiplexer #(.enable("false")) multiplexer_25 (
    .in0(multiplexer_9_out), .in1(multiplexer_11_out), .out(multiplexer_25_out), .sel(Shifter[1]));
  Multiplexer #(.enable("false")) multiplexer_26 (
    .in0(multiplexer_10_out), .in1(multiplexer_12_out), .out(multiplexer_26_out), .sel(Shifter[1]));
  Multiplexer #(.enable("false")) multiplexer_27 (
    .in0(multiplexer_11_out), .in1(multiplexer_13_out), .out(multiplexer_27_out), .sel(Shifter[1]));
  Multiplexer #(.enable("false")) multiplexer_28 (
    .in0(multiplexer_12_out), .in1(multiplexer_14_out), .out(multiplexer_28_out), .sel(Shifter[1]));
  Multiplexer #(.enable("false")) multiplexer_29 (
    .in0(multiplexer_13_out), .in1(multiplexer_15_out), .out(multiplexer_29_out), .sel(Shifter[1]));
  Multiplexer #(.enable("false")) multiplexer_30 (
    .in0(multiplexer_14_out), .in1(multiplexer_16_out), .out(multiplexer_30_out), .sel(Shifter[1]));
  Multiplexer #(.enable("false")) multiplexer_31 (
    .in0(multiplexer_15_out), .in1(1'b0), .out(multiplexer_31_out), .sel(Shifter[1]));
  Multiplexer #(.enable("false")) multiplexer_32 (
    .in0(multiplexer_16_out), .in1(1'b0), .out(multiplexer_32_out), .sel(Shifter[1]));
  Multiplexer #(.enable("false")) multiplexer_33 (
    .in0(multiplexer_17_out), .in1(multiplexer_21_out), .out(Dataout[15]), .sel(Shifter[2]));
  Multiplexer #(.enable("false")) multiplexer_34 (
    .in0(multiplexer_18_out), .in1(multiplexer_22_out), .out(Dataout[14]), .sel(Shifter[2]));
  Multiplexer #(.enable("false")) multiplexer_35 (
    .in0(multiplexer_19_out), .in1(multiplexer_23_out), .out(Dataout[13]), .sel(Shifter[2]));
  Multiplexer #(.enable("false")) multiplexer_36 (
    .in0(multiplexer_20_out), .in1(multiplexer_24_out), .out(Dataout[12]), .sel(Shifter[2]));
  Multiplexer #(.enable("false")) multiplexer_37 (
    .in0(multiplexer_21_out), .in1(multiplexer_25_out), .out(Dataout[11]), .sel(Shifter[2]));
  Multiplexer #(.enable("false")) multiplexer_38 (
    .in0(multiplexer_22_out), .in1(multiplexer_26_out), .out(Dataout[10]), .sel(Shifter[2]));
  Multiplexer #(.enable("false")) multiplexer_39 (
    .in0(multiplexer_23_out), .in1(multiplexer_27_out), .out(Dataout[9]), .sel(Shifter[2]));
  Multiplexer #(.enable("false")) multiplexer_40 (
    .in0(multiplexer_24_out), .in1(multiplexer_28_out), .out(Dataout[8]), .sel(Shifter[2]));
  Multiplexer #(.enable("false")) multiplexer_41 (
    .in0(multiplexer_25_out), .in1(multiplexer_29_out), .out(Dataout[7]), .sel(Shifter[2]));
  Multiplexer #(.enable("false")) multiplexer_42 (
    .in0(multiplexer_26_out), .in1(multiplexer_30_out), .out(Dataout[6]), .sel(Shifter[2]));
  Multiplexer #(.enable("false")) multiplexer_43 (
    .in0(multiplexer_27_out), .in1(multiplexer_31_out), .out(Dataout[5]), .sel(Shifter[2]));
  Multiplexer #(.enable("false")) multiplexer_44 (
    .in0(multiplexer_28_out), .in1(multiplexer_32_out), .out(Dataout[4]), .sel(Shifter[2]));
  Multiplexer #(.enable("false")) multiplexer_45 (
    .in0(multiplexer_29_out), .in1(1'b0), .out(Dataout[3]), .sel(Shifter[2]));
  Multiplexer #(.enable("false")) multiplexer_46 (
    .in0(multiplexer_30_out), .in1(1'b0), .out(Dataout[2]), .sel(Shifter[2]));
  Multiplexer #(.enable("false")) multiplexer_47 (
    .in0(multiplexer_31_out), .in1(1'b0), .out(Dataout[1]), .sel(Shifter[2]));
  Multiplexer #(.enable("false")) multiplexer_48 (
    .in0(multiplexer_32_out), .in1(1'b0), .out(Dataout[0]), .sel(Shifter[2]));

  // Other names for the same wires on the sheet: a0 = Datain[0]; a1 = Datain[1]; a2 = Datain[2]; a3 = Datain[3];
  //   a4 = Datain[4]; a5 = Datain[5]; a6 = Datain[6]; a7 = Datain[7]; a8 = Datain[8]; a9 = Datain[9];
  //   a10 = Datain[10]; a11 = Datain[11]; a12 = Datain[12]; a13 = Datain[13]; a14 = Datain[14]; a15 = Datain[15];
  //   b0 = Dataout[0]; b1 = Dataout[1]; b2 = Dataout[2]; b3 = Dataout[3]; b4 = Dataout[4]; b5 = Dataout[5];
  //   b6 = Dataout[6]; b7 = Dataout[7]; b8 = Dataout[8]; b9 = Dataout[9]; b10 = Dataout[10]; b11 = Dataout[11];
  //   b12 = Dataout[12]; b13 = Dataout[13]; b14 = Dataout[14]; b15 = Dataout[15]; sh1 = Shifter[0]; sh2 = Shifter[1];
  //   sh3 = Shifter[2]
endmodule

module shiftRight (
  input  [2:0] Shifter,
  input  [15:0] Datain,
  output [15:0] Dataout
);

  wire multiplexer_1_out, multiplexer_2_out, multiplexer_3_out, multiplexer_4_out, multiplexer_5_out,
       multiplexer_6_out, multiplexer_7_out, multiplexer_8_out, multiplexer_9_out, multiplexer_10_out,
       multiplexer_11_out, multiplexer_12_out, multiplexer_13_out, multiplexer_14_out, multiplexer_15_out,
       multiplexer_16_out, multiplexer_17_out, multiplexer_18_out, multiplexer_19_out, multiplexer_20_out,
       multiplexer_21_out, multiplexer_22_out, multiplexer_23_out, multiplexer_24_out, multiplexer_25_out,
       multiplexer_26_out, multiplexer_27_out, multiplexer_28_out, multiplexer_29_out, multiplexer_30_out,
       multiplexer_31_out, multiplexer_32_out;

  Multiplexer #(.enable("false")) multiplexer_1 (
    .in0(Datain[0]), .in1(Datain[1]), .out(multiplexer_1_out), .sel(Shifter[0]));
  Multiplexer #(.enable("false")) multiplexer_2 (
    .in0(Datain[1]), .in1(Datain[2]), .out(multiplexer_2_out), .sel(Shifter[0]));
  Multiplexer #(.enable("false")) multiplexer_3 (
    .in0(Datain[2]), .in1(Datain[3]), .out(multiplexer_3_out), .sel(Shifter[0]));
  Multiplexer #(.enable("false")) multiplexer_4 (
    .in0(Datain[3]), .in1(Datain[4]), .out(multiplexer_4_out), .sel(Shifter[0]));
  Multiplexer #(.enable("false")) multiplexer_5 (
    .in0(Datain[4]), .in1(Datain[5]), .out(multiplexer_5_out), .sel(Shifter[0]));
  Multiplexer #(.enable("false")) multiplexer_6 (
    .in0(Datain[5]), .in1(Datain[6]), .out(multiplexer_6_out), .sel(Shifter[0]));
  Multiplexer #(.enable("false")) multiplexer_7 (
    .in0(Datain[6]), .in1(Datain[7]), .out(multiplexer_7_out), .sel(Shifter[0]));
  Multiplexer #(.enable("false")) multiplexer_8 (
    .in0(Datain[7]), .in1(Datain[8]), .out(multiplexer_8_out), .sel(Shifter[0]));
  Multiplexer #(.enable("false")) multiplexer_9 (
    .in0(Datain[8]), .in1(Datain[9]), .out(multiplexer_9_out), .sel(Shifter[0]));
  Multiplexer #(.enable("false")) multiplexer_10 (
    .in0(Datain[9]), .in1(Datain[10]), .out(multiplexer_10_out), .sel(Shifter[0]));
  Multiplexer #(.enable("false")) multiplexer_11 (
    .in0(Datain[10]), .in1(Datain[11]), .out(multiplexer_11_out), .sel(Shifter[0]));
  Multiplexer #(.enable("false")) multiplexer_12 (
    .in0(Datain[11]), .in1(Datain[12]), .out(multiplexer_12_out), .sel(Shifter[0]));
  Multiplexer #(.enable("false")) multiplexer_13 (
    .in0(Datain[12]), .in1(Datain[13]), .out(multiplexer_13_out), .sel(Shifter[0]));
  Multiplexer #(.enable("false")) multiplexer_14 (
    .in0(Datain[13]), .in1(Datain[14]), .out(multiplexer_14_out), .sel(Shifter[0]));
  Multiplexer #(.enable("false")) multiplexer_15 (
    .in0(Datain[14]), .in1(Datain[15]), .out(multiplexer_15_out), .sel(Shifter[0]));
  Multiplexer #(.enable("false")) multiplexer_16 (
    .in0(Datain[15]), .in1(1'b0), .out(multiplexer_16_out), .sel(Shifter[0]));
  Multiplexer #(.enable("false")) multiplexer_17 (
    .in0(multiplexer_1_out), .in1(multiplexer_3_out), .out(multiplexer_17_out), .sel(Shifter[1]));
  Multiplexer #(.enable("false")) multiplexer_18 (
    .in0(multiplexer_2_out), .in1(multiplexer_4_out), .out(multiplexer_18_out), .sel(Shifter[1]));
  Multiplexer #(.enable("false")) multiplexer_19 (
    .in0(multiplexer_3_out), .in1(multiplexer_5_out), .out(multiplexer_19_out), .sel(Shifter[1]));
  Multiplexer #(.enable("false")) multiplexer_20 (
    .in0(multiplexer_4_out), .in1(multiplexer_6_out), .out(multiplexer_20_out), .sel(Shifter[1]));
  Multiplexer #(.enable("false")) multiplexer_21 (
    .in0(multiplexer_5_out), .in1(multiplexer_7_out), .out(multiplexer_21_out), .sel(Shifter[1]));
  Multiplexer #(.enable("false")) multiplexer_22 (
    .in0(multiplexer_6_out), .in1(multiplexer_8_out), .out(multiplexer_22_out), .sel(Shifter[1]));
  Multiplexer #(.enable("false")) multiplexer_23 (
    .in0(multiplexer_7_out), .in1(multiplexer_9_out), .out(multiplexer_23_out), .sel(Shifter[1]));
  Multiplexer #(.enable("false")) multiplexer_24 (
    .in0(multiplexer_8_out), .in1(multiplexer_10_out), .out(multiplexer_24_out), .sel(Shifter[1]));
  Multiplexer #(.enable("false")) multiplexer_25 (
    .in0(multiplexer_9_out), .in1(multiplexer_11_out), .out(multiplexer_25_out), .sel(Shifter[1]));
  Multiplexer #(.enable("false")) multiplexer_26 (
    .in0(multiplexer_10_out), .in1(multiplexer_12_out), .out(multiplexer_26_out), .sel(Shifter[1]));
  Multiplexer #(.enable("false")) multiplexer_27 (
    .in0(multiplexer_11_out), .in1(multiplexer_13_out), .out(multiplexer_27_out), .sel(Shifter[1]));
  Multiplexer #(.enable("false")) multiplexer_28 (
    .in0(multiplexer_12_out), .in1(multiplexer_14_out), .out(multiplexer_28_out), .sel(Shifter[1]));
  Multiplexer #(.enable("false")) multiplexer_29 (
    .in0(multiplexer_13_out), .in1(multiplexer_15_out), .out(multiplexer_29_out), .sel(Shifter[1]));
  Multiplexer #(.enable("false")) multiplexer_30 (
    .in0(multiplexer_14_out), .in1(multiplexer_16_out), .out(multiplexer_30_out), .sel(Shifter[1]));
  Multiplexer #(.enable("false")) multiplexer_31 (
    .in0(multiplexer_15_out), .in1(1'b0), .out(multiplexer_31_out), .sel(Shifter[1]));
  Multiplexer #(.enable("false")) multiplexer_32 (
    .in0(multiplexer_16_out), .in1(1'b0), .out(multiplexer_32_out), .sel(Shifter[1]));
  Multiplexer #(.enable("false")) multiplexer_33 (
    .in0(multiplexer_17_out), .in1(multiplexer_21_out), .out(Dataout[0]), .sel(Shifter[2]));
  Multiplexer #(.enable("false")) multiplexer_34 (
    .in0(multiplexer_18_out), .in1(multiplexer_22_out), .out(Dataout[1]), .sel(Shifter[2]));
  Multiplexer #(.enable("false")) multiplexer_35 (
    .in0(multiplexer_19_out), .in1(multiplexer_23_out), .out(Dataout[2]), .sel(Shifter[2]));
  Multiplexer #(.enable("false")) multiplexer_36 (
    .in0(multiplexer_20_out), .in1(multiplexer_24_out), .out(Dataout[3]), .sel(Shifter[2]));
  Multiplexer #(.enable("false")) multiplexer_37 (
    .in0(multiplexer_21_out), .in1(multiplexer_25_out), .out(Dataout[4]), .sel(Shifter[2]));
  Multiplexer #(.enable("false")) multiplexer_38 (
    .in0(multiplexer_22_out), .in1(multiplexer_26_out), .out(Dataout[5]), .sel(Shifter[2]));
  Multiplexer #(.enable("false")) multiplexer_39 (
    .in0(multiplexer_23_out), .in1(multiplexer_27_out), .out(Dataout[6]), .sel(Shifter[2]));
  Multiplexer #(.enable("false")) multiplexer_40 (
    .in0(multiplexer_24_out), .in1(multiplexer_28_out), .out(Dataout[7]), .sel(Shifter[2]));
  Multiplexer #(.enable("false")) multiplexer_41 (
    .in0(multiplexer_25_out), .in1(multiplexer_29_out), .out(Dataout[8]), .sel(Shifter[2]));
  Multiplexer #(.enable("false")) multiplexer_42 (
    .in0(multiplexer_26_out), .in1(multiplexer_30_out), .out(Dataout[9]), .sel(Shifter[2]));
  Multiplexer #(.enable("false")) multiplexer_43 (
    .in0(multiplexer_27_out), .in1(multiplexer_31_out), .out(Dataout[10]), .sel(Shifter[2]));
  Multiplexer #(.enable("false")) multiplexer_44 (
    .in0(multiplexer_28_out), .in1(multiplexer_32_out), .out(Dataout[11]), .sel(Shifter[2]));
  Multiplexer #(.enable("false")) multiplexer_45 (
    .in0(multiplexer_29_out), .in1(1'b0), .out(Dataout[12]), .sel(Shifter[2]));
  Multiplexer #(.enable("false")) multiplexer_46 (
    .in0(multiplexer_30_out), .in1(1'b0), .out(Dataout[13]), .sel(Shifter[2]));
  Multiplexer #(.enable("false")) multiplexer_47 (
    .in0(multiplexer_31_out), .in1(1'b0), .out(Dataout[14]), .sel(Shifter[2]));
  Multiplexer #(.enable("false")) multiplexer_48 (
    .in0(multiplexer_32_out), .in1(1'b0), .out(Dataout[15]), .sel(Shifter[2]));

  // Other names for the same wires on the sheet: a0 = Datain[0]; a1 = Datain[1]; a2 = Datain[2]; a3 = Datain[3];
  //   a4 = Datain[4]; a5 = Datain[5]; a6 = Datain[6]; a7 = Datain[7]; a8 = Datain[8]; a9 = Datain[9];
  //   a10 = Datain[10]; a11 = Datain[11]; a12 = Datain[12]; a13 = Datain[13]; a14 = Datain[14]; a15 = Datain[15];
  //   b0 = Dataout[0]; b1 = Dataout[1]; b2 = Dataout[2]; b3 = Dataout[3]; b4 = Dataout[4]; b5 = Dataout[5];
  //   b6 = Dataout[6]; b7 = Dataout[7]; b8 = Dataout[8]; b9 = Dataout[9]; b10 = Dataout[10]; b11 = Dataout[11];
  //   b12 = Dataout[12]; b13 = Dataout[13]; b14 = Dataout[14]; b15 = Dataout[15]; sh1 = Shifter[0]; sh2 = Shifter[1];
  //   sh3 = Shifter[2]
endmodule
